# Fritzing sketch wiring (saved by Fritzing 0.9.3b)
breadboards: 1

parts:
  Composant1 = Arduino Nano (Rev3.0)
  hc-sr1 = hc-sr04
  VCC1 = Battery block 9V
  Composant2 = Arduino Motor Shield
  M1 = DC Motor
  M2 = DC Motor
  IC1 = Voltage Regulator [package=to220-igo]
  VCC2 = Battery block 9V
  J1 = Basic Servo

nets:
  GND: Composant1.GND, hc-sr1.GND, IC1.GND, VCC2.-, J1.gnd
  N1: Composant1.D2, hc-sr1.Trig
  N2: Composant1.D3, hc-sr1.Echo
  N3: Composant1.D4, Composant2.D12
  N4: Composant1.D5, Composant2.D5
  N5: Composant1.D6, Composant2.D13
  N6: Composant1.D7, Composant2.D6
  N7: Composant1.D8, J1.pulse
  N8: Composant1.D9, Composant2.D11
  N9: Composant1.D10, Composant2.D3
  N10: Composant1.VIN, IC1.OUT
  VCC: Composant1.5V, hc-sr1.VCC, J1.vcc
  N11: VCC1.-, Composant2.GND
  N12: VCC1.+, Composant2.VIN
  N13: Composant2.OUT3, M2.pin_2
  N14: Composant2.OUT4, M2.pin_1
  N15: Composant2.OUT2, M1.pin_2
  N16: Composant2.OUT1, M1.pin_1
  N17: IC1.IN, VCC2.+

notes:
  This is not the exact component. But looks like it.
  Used one is L298.
